# Fritzing sketch Schemat elektryczny (saved by Fritzing 0.9.3b)
breadboards: 1

parts:
  Part2 = Arduino Uno (Rev3)
  VCC1 = Battery
  C1 = Ceramic Capacitor [capacitance=100nF package="100 mil [THT, multilayer]"]
  C2 = Ceramic Capacitor [capacitance=100nF package="100 mil [THT, multilayer]"]

nets:
  N1: Part2.D8, Part2.D9_PWM, Part2.D10_PWM/SS, Part2.D11_PWM/MOSI
  N2: Part2.D2, Part2.D3_PWM, Part2.D4, Part2.D5_PWM
  N3: VCC1.-, C1.1, C2.0
  N4: VCC1.+, C2.1

notes:
  Zasilanie 7,4V
  Zasilanie 6V
  Przetwornica step-down 6V 15A - Pololu - D24V150F6
  Sterownik TB9051FTG
